# Fritzing sketch Indoor Watering System Schematic (saved by Fritzing 0.9.3b)

parts:
  Part1 = Arduino Mega 2560 (Rev3)
  U1 = RELAY [package=relay-g5q]
  Part2 = Soil Moisture Sensor
  Power_plug1 = Power plug  # not connected
  M1 = DC Motor  # not connected
  VCC1 = 4 x AAA Battery Mount  # not connected

nets:
  N1: Part1.D13_PWM, U1.COIL1
  N2: Part1.D8_PWM, Part2.SIG
  5V: Part1.5V, Part2.VCC
  GND: Part1.GND, U1.COIL2, Part2.GND

notes:
  12V Water Pump
  5V Power Source
